# Fritzing sketch Embedded Systems (saved by Fritzing 0.9.3b)
breadboards: 1

parts:
  Arduino_Uno = Arduino Uno (Rev3)
  R1 = TRIMPOT [package=trimpot-3mm]
  U1 = LCD-16X2 [package=lcd-16x2]
  R2 = Resistor [tolerance=±5% resistance=1k package=THT]
  LED1 = LED - 5mm [color="Red (633nm)" package="5 mm [THT]"]  # not connected

nets:
  N1: Arduino_Uno.A0, U1.E
  N2: Arduino_Uno.A1, U1.RS
  N3: Arduino_Uno.A2, U1.DB7
  N4: Arduino_Uno.A3, U1.DB6
  N5: Arduino_Uno.A4/SDA, U1.DB5
  N6: Arduino_Uno.A5/SCL, U1.DB4
  GND: Arduino_Uno.GND, R1.WIPER, U1.VSS, U1.R_W, U1.K
  5V: Arduino_Uno.5V, R1.CCW, U1.VDD, R2.Pin_1
  N7: R1.CW, U1.VO
  N8: U1.A, R2.Pin_0
