# Fritzing sketch bttnBlinkLED (saved by Fritzing 0.9.3b)
breadboards: 1

parts:
  Arduino_Uno = Arduino Uno (Rev3)
  S1 = Pushbutton [package="[THT]"]
  R1 = Resistor [tolerance=±20% resistance=1k package=THT]
  LED1 = LED - 5mm [color="Blue (430nm)" package="5 mm [THT]"]
  R2 = Resistor [tolerance=±20% resistance=1k package=THT]

nets:
  N1: Arduino_Uno.D13/SCK, LED1.anode
  N2: Arduino_Uno.GND, R1.Pin_1, R2.Pin_0
  N3: Arduino_Uno.D7, S1.Pin_1, S1.Pin_2, R1.Pin_0
  N4: Arduino_Uno.5V, S1.Pin_3, S1.Pin_4
  N5: LED1.cathode, R2.Pin_1

// code stored in the sketch: bttnBlinkLED.ino
/*  With a push on the button the LED will turn on/off,
 *  holding it's current state until the button is pressed again
 */

#define LED 13
#define BUTTON 7

bool isLEDOn = false;
bool val, old_val = false;

void setup () {
  pinMode(LED,OUTPUT);
  pinMode(BUTTON, INPUT);
}

void loop (){
  val = digitalRead(BUTTON);
  
  if(val && !old_val) {
    isLEDOn = !isLEDOn;
  }

  old_val = val;
  switchLED(isLEDOn);
}

void switchLED(bool LED_state){
  digitalWrite(LED, LED_state ? HIGH : LOW);
}
